// Logisim project 721615-cache.circ as structural Verilog: 1 circuit, main circuit main
module main (
  input  in_1,
  input  in_2,
  output [31:0] out_3
);

  wire act_remp, and_1_out, clk, comparator_1_eq, comparator_2_eq, comparator_3_eq, comparator_4_eq,
       comparator_5_eq, cont_en1_2_3_4, cont_en5_6_7_8, decoder_1_out0, decoder_1_out1, hit, mem_en,
       not_1_out, not_2_out, q0, q1, q2, q3, ram_6_data, way, write;
  wire [1:0] rom_1_data, word;
  wire [2:0] reg_en;
  wire [3:0] rom_2_data;
  wire [4:0] set;
  wire [6:0] tag;
  wire [7:0] counter_1_q, ram_10_data, ram_11_data;
  wire [31:0] main_1_p4, multiplexer_1_out, multiplexer_3_out, ram_1_data, ram_2_data, ram_3_data,
       ram_4_data, ram_5_data, ram_7_data, ram_8_data, ram_9_data, Reg1, Reg2, Reg3, Reg4;

  Clock clock_1 (.out(clk));
  RAM #(.addrWidth(5), .dataWidth(32), .bus("separate")) ram_1 (
    .addr(set), .din(Reg1), .data(ram_1_data), .str(cont_en1_2_3_4), .clk(clk), .clr(in_1));  // open: sel, ld
  Counter counter_1 (.count(hit), .Q(counter_1_q), .clk(clk), .clr(in_2));  // open: load, D, carry
  RAM #(.addrWidth(5), .dataWidth(32), .bus("separate")) ram_2 (
    .addr(set), .din(Reg2), .data(ram_2_data), .str(cont_en1_2_3_4), .clk(clk), .clr(in_1));  // open: sel, ld
  Multiplexer #(.select(2), .width(32), .enable("false")) multiplexer_1 (
    .in0(ram_1_data), .in1(ram_2_data), .in2(ram_3_data), .in3(ram_4_data), .out(multiplexer_1_out),
    .sel(word));
  ROM #(.dataWidth(16)) rom_1 (.addr(counter_1_q), .data({tag, set, word, rom_1_data}));  // open: sel
  // MP_main main_1: pin names not known; wires that end beside it: {tag, set, word, rom_1_data}, mem_en, clk, main_1_p4
  RAM #(.addrWidth(5), .dataWidth(32), .bus("separate")) ram_3 (
    .addr(set), .din(Reg3), .data(ram_3_data), .str(cont_en1_2_3_4), .clk(clk), .clr(in_1));  // open: sel, ld
  Comparator #(.width(3)) comparator_1 (.a(reg_en), .b(3'b001), .eq(comparator_1_eq));  // open: gt, lt
  Comparator #(.width(3)) comparator_2 (.a(reg_en), .b(3'b010), .eq(comparator_2_eq));  // open: gt, lt
  Comparator #(.width(3)) comparator_3 (.a(reg_en), .b(3'b011), .eq(comparator_3_eq));  // open: gt, lt
  Comparator #(.width(3)) comparator_4 (.a(reg_en), .b(3'b100), .eq(comparator_4_eq));  // open: gt, lt
  Register #(.width(32)) register_1 (.D(main_1_p4), .en(comparator_1_eq), .Q(Reg1), .clk(clk), .clr(in_2));
  Register #(.width(32)) register_2 (.D(main_1_p4), .en(comparator_2_eq), .Q(Reg2), .clk(clk), .clr(in_2));
  Register #(.width(32)) register_3 (.D(main_1_p4), .en(comparator_3_eq), .Q(Reg3), .clk(clk), .clr(in_2));
  Register #(.width(32)) register_4 (.D(main_1_p4), .en(comparator_4_eq), .Q(Reg4), .clk(clk), .clr(in_2));
  RAM #(.addrWidth(5), .dataWidth(32), .bus("separate")) ram_4 (
    .addr(set), .din(Reg4), .data(ram_4_data), .str(cont_en1_2_3_4), .clk(clk), .clr(in_1));  // open: sel, ld
  Multiplexer #(.width(32), .enable("false")) multiplexer_2 (
    .in0(multiplexer_1_out), .in1(multiplexer_3_out), .out(out_3), .sel(way));
  RAM #(.addrWidth(5), .dataWidth(32), .bus("separate")) ram_5 (
    .addr(set), .din(Reg1), .data(ram_5_data), .str(cont_en5_6_7_8), .clk(clk));  // open: sel, ld, clr
  not not_1 (not_1_out, act_remp);
  not not_2 (not_2_out, ram_6_data);
  RAM #(.addrWidth(5), .dataWidth(1), .bus("separate")) ram_6 (
    .addr(set), .din(not_2_out), .data(ram_6_data), .str(not_1_out), .clk(clk), .clr(in_1));  // open: sel, ld
  ROM #(.addrWidth(5), .dataWidth(4)) rom_2 (.addr({q3, q2, q1, q0, hit}), .data(rom_2_data));  // open: sel
  RAM #(.addrWidth(5), .dataWidth(32), .bus("separate")) ram_7 (
    .addr(set), .din(Reg2), .data(ram_7_data), .str(cont_en5_6_7_8), .clk(clk), .clr(in_1));  // open: sel, ld
  Multiplexer #(.select(2), .width(32), .enable("false")) multiplexer_3 (
    .in0(ram_5_data), .in1(ram_7_data), .in2(ram_8_data), .in3(ram_9_data), .out(multiplexer_3_out),
    .sel(word));
  and and_1 (and_1_out, write, ram_6_data);
  Register #(.width(4)) register_5 (.D(rom_2_data), .Q({q3, q2, q1, q0}), .clk(clk), .clr(in_2));  // open: en
  Decoder #(.enable("false")) decoder_1 (.out0(decoder_1_out0), .out1(decoder_1_out1), .sel(and_1_out));
  RAM #(.addrWidth(5), .dataWidth(32), .bus("separate")) ram_8 (
    .addr(set), .din(Reg3), .data(ram_8_data), .str(cont_en5_6_7_8), .clk(clk), .clr(in_1));  // open: sel, ld
  and and_2 (cont_en1_2_3_4, write, decoder_1_out0);
  and and_3 (cont_en5_6_7_8, decoder_1_out1, write);
  ROM #(.addrWidth(4), .dataWidth(6)) rom_3 (
    .addr({q3, q2, q1, q0}), .data({mem_en, reg_en, act_remp, write}));  // open: sel
  RAM #(.addrWidth(5), .dataWidth(32), .bus("separate")) ram_9 (
    .addr(set), .din(Reg4), .data(ram_9_data), .str(cont_en5_6_7_8), .clk(clk), .clr(in_1));  // open: sel, ld
  RAM #(.addrWidth(5), .bus("separate")) ram_10 (
    .addr(set), .din({tag, 1'b1}), .data(ram_10_data), .str(cont_en1_2_3_4), .clk(clk), .clr(in_1));  // open: sel, ld
  Comparator comparator_5 (.a(ram_10_data), .b({tag, 1'b1}), .eq(comparator_5_eq));  // open: gt, lt
  or or_1 (hit, comparator_5_eq, way);
  RAM #(.addrWidth(5), .bus("separate")) ram_11 (
    .addr(set), .din({tag, 1'b1}), .data(ram_11_data), .str(cont_en5_6_7_8), .clk(clk), .clr(in_1));  // open: sel, ld
  Comparator comparator_6 (.a(ram_11_data), .b({tag, 1'b1}), .eq(way));  // open: gt, lt

  // Other names for the same wires on the sheet: clrRAM = in_1; inst[31:0] = out_3; reset = in_2

  // Notes on the sheet:
  //   1
  //   CONTADOR
  //   2
  //   ROM
  //   contents of rom_1 (hex, n*v repeats v):
  //   4 200 400 204 180 380 780 784 6c0c 1408 404 408
  //   3
  //   MP
  //   4
  //   5
  //   6
  //   contents of rom_2 (hex, n*v repeats v):
  //   1 0 2 2 3 3 d d 5 5 6 6 7 7 8 8 9 9 a a b b 4*0 4 4
  //   7
  //   contents of rom_3 (hex, n*v repeats v):
  //   2 22 22 22 26 22 2a 22 2e 22 32 21 0 22
  //   8
  //   TAG1-2-3-4
  //   TAG5-6-7-8
endmodule
