// Logisim project 721615-multi.circ as structural Verilog: 3 circuits, main circuit PROC1
module BR4 (
  input  [31:0] busW,
  input  [1:0] RA,
  input  [1:0] RW,
  input  RegWr,
  input  [1:0] RB,
  input  clk,
  input  reset,
  output [31:0] busA,
  output [31:0] busB
);

  wire and_1_out, and_2_out, and_3_out, and_4_out, decoder_1_out0, decoder_1_out1, decoder_1_out2,
       decoder_1_out3;
  wire [31:0] register_1_q, register_2_q, register_3_q, register_4_q;

  Decoder #(.select(2), .enable("false")) decoder_1 (
    .out0(decoder_1_out0), .out1(decoder_1_out1), .out2(decoder_1_out2), .out3(decoder_1_out3), .sel(RW));
  and and_1 (and_1_out, RegWr, decoder_1_out0);
  and and_2 (and_2_out, RegWr, decoder_1_out1);
  and and_3 (and_3_out, RegWr, decoder_1_out2);
  and and_4 (and_4_out, RegWr, decoder_1_out3);
  Register #(.width(32)) register_1 (.D(busW), .en(and_1_out), .Q(register_1_q), .clk(clk), .clr(reset));
  Register #(.width(32)) register_2 (.D(busW), .en(and_2_out), .Q(register_2_q), .clk(clk), .clr(reset));
  Register #(.width(32)) register_3 (.D(busW), .en(and_3_out), .Q(register_3_q), .clk(clk), .clr(reset));
  Register #(.width(32)) register_4 (.D(busW), .en(and_4_out), .Q(register_4_q), .clk(clk), .clr(reset));
  Multiplexer #(.select(2), .width(32), .enable("false")) multiplexer_1 (
    .in0(register_1_q), .in1(register_2_q), .in2(register_3_q), .in3(register_4_q), .out(busA), .sel(RA));
  Multiplexer #(.select(2), .width(32), .enable("false")) multiplexer_2 (
    .in0(register_1_q), .in1(register_2_q), .in2(register_3_q), .in3(register_4_q), .out(busB), .sel(RB));
endmodule

module BR32 (
  input  RegWr,
  input  [4:0] RA,
  input  [4:0] RB,
  input  [4:0] RW,
  input  [31:0] busW,
  input  reset,
  input  clk,
  output [31:0] busA,
  output [31:0] busB
);

  wire and_1_out, and_2_out, and_3_out, and_4_out, and_5_out, and_6_out, and_7_out, and_8_out,
       decoder_1_out0, decoder_1_out1, decoder_1_out2, decoder_1_out3, decoder_1_out4, decoder_1_out5,
       decoder_1_out6, decoder_1_out7;
  wire [31:0] br4_1_busa, br4_1_busb, br4_2_busa, br4_2_busb, br4_3_busa, br4_3_busb, br4_4_busa, br4_4_busb,
       br4_5_busa, br4_5_busb, br4_6_busa, br4_6_busb, br4_7_busa, br4_7_busb, br4_8_busa, br4_8_busb;

  Decoder #(.select(3), .enable("false")) decoder_1 (
    .out0(decoder_1_out0), .out1(decoder_1_out1), .out2(decoder_1_out2), .out3(decoder_1_out3),
    .out4(decoder_1_out4), .out5(decoder_1_out5), .out6(decoder_1_out6), .out7(decoder_1_out7), .sel(RW[4:2]));
  and and_1 (and_1_out, RegWr, decoder_1_out0);
  and and_2 (and_2_out, RegWr, decoder_1_out1);
  and and_3 (and_3_out, RegWr, decoder_1_out2);
  and and_4 (and_4_out, RegWr, decoder_1_out3);
  and and_5 (and_5_out, RegWr, decoder_1_out4);
  and and_6 (and_6_out, RegWr, decoder_1_out5);
  and and_7 (and_7_out, RegWr, decoder_1_out6);
  and and_8 (and_8_out, RegWr, decoder_1_out7);
  BR4 br4_1 (
    .busW(busW), .RA(RA[1:0]), .RW(RW[1:0]), .RegWr(and_1_out), .RB(RB[1:0]), .clk(clk), .reset(reset),
    .busA(br4_1_busa), .busB(br4_1_busb));
  BR4 br4_2 (
    .busW(busW), .RA(RA[1:0]), .RW(RW[1:0]), .RegWr(and_2_out), .RB(RB[1:0]), .clk(clk), .reset(reset),
    .busA(br4_2_busa), .busB(br4_2_busb));
  BR4 br4_3 (
    .busW(busW), .RA(RA[1:0]), .RW(RW[1:0]), .RegWr(and_3_out), .RB(RB[1:0]), .clk(clk), .reset(reset),
    .busA(br4_3_busa), .busB(br4_3_busb));
  BR4 br4_4 (
    .busW(busW), .RA(RA[1:0]), .RW(RW[1:0]), .RegWr(and_4_out), .RB(RB[1:0]), .clk(clk), .reset(reset),
    .busA(br4_4_busa), .busB(br4_4_busb));
  BR4 br4_5 (
    .busW(busW), .RA(RA[1:0]), .RW(RW[1:0]), .RegWr(and_5_out), .RB(RB[1:0]), .clk(clk), .reset(reset),
    .busA(br4_5_busa), .busB(br4_5_busb));
  BR4 br4_6 (
    .busW(busW), .RA(RA[1:0]), .RW(RW[1:0]), .RegWr(and_6_out), .RB(RB[1:0]), .clk(clk), .reset(reset),
    .busA(br4_6_busa), .busB(br4_6_busb));
  BR4 br4_7 (
    .busW(busW), .RA(RA[1:0]), .RW(RW[1:0]), .RegWr(and_7_out), .RB(RB[1:0]), .clk(clk), .reset(reset),
    .busA(br4_7_busa), .busB(br4_7_busb));
  BR4 br4_8 (
    .busW(busW), .RA(RA[1:0]), .RW(RW[1:0]), .RegWr(and_8_out), .RB(RB[1:0]), .clk(clk), .reset(reset),
    .busA(br4_8_busa), .busB(br4_8_busb));
  Multiplexer #(.select(3), .width(32), .enable("false")) multiplexer_1 (
    .in0(br4_1_busa), .in1(br4_2_busa), .in2(br4_3_busa), .in3(br4_4_busa), .in4(br4_5_busa),
    .in5(br4_6_busa), .in6(br4_7_busa), .in7(br4_8_busa), .out(busA), .sel(RA[4:2]));
  Multiplexer #(.select(3), .width(32), .enable("false")) multiplexer_2 (
    .in0(br4_1_busb), .in1(br4_2_busb), .in2(br4_3_busb), .in3(br4_4_busb), .in4(br4_5_busb),
    .in5(br4_6_busb), .in6(br4_7_busb), .in7(br4_8_busb), .out(busB), .sel(RB[4:2]));

  // Other names for the same wires on the sheet: RAmux[2:0] = RA[4:2]; RAreg[1:0] = RA[1:0]; RBmux[2:0] = RB[4:2];
  //   RBreg[1:0] = RB[1:0]; RWdecod[2:0] = RW[4:2]; RWreg[1:0] = RW[1:0]
endmodule

// UC
module PROC1 (
  input  reset
);

  wire clk_out, MUX, NI, q0, q1, RegWr;
  wire [1:0] rom_2_data;
  wire [3:0] counter_1_q;
  wire [21:0] inst;
  wire [31:0] adder_1_out, bit_extender_1_out, br32_1_busa, br32_1_busb, multiplexer_1_out, RA_q, RB_q, RC_q;

  Counter #(.width(4), .max('hf)) counter_1 (
    .count(NI), .Q(counter_1_q), .clk(clk_out), .clr(reset));  // open: load, D, carry
  ROM #(.addrWidth(4), .dataWidth(22)) rom_1 (.addr(counter_1_q), .data(inst));  // open: sel
  assign bit_extender_1_out = {{16{inst[20]}}, inst[20:5]};  // Bit_Extender bit_extender_1
  Multiplexer #(.width(32), .enable("false")) multiplexer_1 (
    .in0(bit_extender_1_out), .in1(RC_q), .out(multiplexer_1_out), .sel(MUX));
  Clock clk (.out(clk_out));
  ROM #(.addrWidth(3), .dataWidth(2)) rom_2 (.addr({q1, q0, inst[21]}), .data(rom_2_data));  // open: sel
  ROM #(.addrWidth(3), .dataWidth(3)) rom_3 (.addr({q1, q0, inst[21]}), .data({MUX, RegWr, NI}));  // open: sel
  BR32 br32_1 (
    .RegWr(RegWr), .RA(inst[14:10]), .RB(inst[9:5]), .RW(inst[4:0]), .busW(multiplexer_1_out), .reset(reset),
    .clk(clk_out), .busA(br32_1_busa), .busB(br32_1_busb));
  Register #(.width(2)) register_1 (.D(rom_2_data), .Q({q1, q0}), .clk(clk_out), .clr(reset));  // open: en
  Register #(.width(32)) RA (.D(br32_1_busa), .Q(RA_q), .clk(clk_out), .clr(reset));  // open: en
  Register #(.width(32)) RB (.D(br32_1_busb), .Q(RB_q), .clk(clk_out), .clr(reset));  // open: en
  Adder #(.width(32)) adder_1 (.a(RA_q), .b(RB_q), .out(adder_1_out));  // open: cin, cout
  Register #(.width(32)) RC (.D(adder_1_out), .Q(RC_q), .clk(clk_out), .clr(reset));  // open: en

  // Other names for the same wires on the sheet: op = inst[21]; k[15:0] = inst[20:5]; ra[4:0] = inst[14:10];
  //   rb[4:0] = inst[9:5]; rd[4:0] = inst[4:0]

  // Notes on the sheet:
  //   contents of rom_1 (hex, n*v repeats v):
  //   e0 41 22 c3 24 a5 200027 200868 2010a6 201d07 201cc6
  //   UC
  //   TT
  //   TS
  //   contents of rom_2 (hex, n*v repeats v):
  //   0 1 2 2
  //   contents of rom_3 (hex, n*v repeats v):
  //   3 0 0 0 7 7
endmodule
