// Logisim project 721615-multi2.circ as structural Verilog: 3 circuits, main circuit PROC1
module BR4 (
  input  [31:0] busW,
  input  [1:0] RA,
  input  [1:0] RW,
  input  RegWr,
  input  [1:0] RB,
  input  clk,
  input  reset,
  output [31:0] busA,
  output [31:0] busB
);

  wire and_1_out, and_2_out, and_3_out, and_4_out, decoder_1_out0, decoder_1_out1, decoder_1_out2,
       decoder_1_out3;
  wire [31:0] register_1_q, register_2_q, register_3_q, register_4_q;

  Decoder #(.select(2), .enable("false")) decoder_1 (
    .out0(decoder_1_out0), .out1(decoder_1_out1), .out2(decoder_1_out2), .out3(decoder_1_out3), .sel(RW));
  and and_1 (and_1_out, RegWr, decoder_1_out0);
  and and_2 (and_2_out, RegWr, decoder_1_out1);
  and and_3 (and_3_out, RegWr, decoder_1_out2);
  and and_4 (and_4_out, RegWr, decoder_1_out3);
  Register #(.width(32)) register_1 (.D(busW), .en(and_1_out), .Q(register_1_q), .clk(clk), .clr(reset));
  Register #(.width(32)) register_2 (.D(busW), .en(and_2_out), .Q(register_2_q), .clk(clk), .clr(reset));
  Register #(.width(32)) register_3 (.D(busW), .en(and_3_out), .Q(register_3_q), .clk(clk), .clr(reset));
  Register #(.width(32)) register_4 (.D(busW), .en(and_4_out), .Q(register_4_q), .clk(clk), .clr(reset));
  Multiplexer #(.select(2), .width(32), .enable("false")) multiplexer_1 (
    .in0(register_1_q), .in1(register_2_q), .in2(register_3_q), .in3(register_4_q), .out(busA), .sel(RA));
  Multiplexer #(.select(2), .width(32), .enable("false")) multiplexer_2 (
    .in0(register_1_q), .in1(register_2_q), .in2(register_3_q), .in3(register_4_q), .out(busB), .sel(RB));
endmodule

module BR32 (
  input  RegWr,
  input  [4:0] RA,
  input  [4:0] RB,
  input  [4:0] RW,
  input  [31:0] busW,
  input  reset,
  input  clk,
  output [31:0] busA,
  output [31:0] busB
);

  wire and_1_out, and_2_out, and_3_out, and_4_out, and_5_out, and_6_out, and_7_out, and_8_out,
       decoder_1_out0, decoder_1_out1, decoder_1_out2, decoder_1_out3, decoder_1_out4, decoder_1_out5,
       decoder_1_out6, decoder_1_out7;
  wire [31:0] br4_1_busa, br4_1_busb, br4_2_busa, br4_2_busb, br4_3_busa, br4_3_busb, br4_4_busa, br4_4_busb,
       br4_5_busa, br4_5_busb, br4_6_busa, br4_6_busb, br4_7_busa, br4_7_busb, br4_8_busa, br4_8_busb;

  Decoder #(.select(3), .enable("false")) decoder_1 (
    .out0(decoder_1_out0), .out1(decoder_1_out1), .out2(decoder_1_out2), .out3(decoder_1_out3),
    .out4(decoder_1_out4), .out5(decoder_1_out5), .out6(decoder_1_out6), .out7(decoder_1_out7), .sel(RW[4:2]));
  and and_1 (and_1_out, RegWr, decoder_1_out0);
  and and_2 (and_2_out, RegWr, decoder_1_out1);
  and and_3 (and_3_out, RegWr, decoder_1_out2);
  and and_4 (and_4_out, RegWr, decoder_1_out3);
  and and_5 (and_5_out, RegWr, decoder_1_out4);
  and and_6 (and_6_out, RegWr, decoder_1_out5);
  and and_7 (and_7_out, RegWr, decoder_1_out6);
  and and_8 (and_8_out, RegWr, decoder_1_out7);
  BR4 br4_1 (
    .busW(busW), .RA(RA[1:0]), .RW(RW[1:0]), .RegWr(and_1_out), .RB(RB[1:0]), .clk(clk), .reset(reset),
    .busA(br4_1_busa), .busB(br4_1_busb));
  BR4 br4_2 (
    .busW(busW), .RA(RA[1:0]), .RW(RW[1:0]), .RegWr(and_2_out), .RB(RB[1:0]), .clk(clk), .reset(reset),
    .busA(br4_2_busa), .busB(br4_2_busb));
  BR4 br4_3 (
    .busW(busW), .RA(RA[1:0]), .RW(RW[1:0]), .RegWr(and_3_out), .RB(RB[1:0]), .clk(clk), .reset(reset),
    .busA(br4_3_busa), .busB(br4_3_busb));
  BR4 br4_4 (
    .busW(busW), .RA(RA[1:0]), .RW(RW[1:0]), .RegWr(and_4_out), .RB(RB[1:0]), .clk(clk), .reset(reset),
    .busA(br4_4_busa), .busB(br4_4_busb));
  BR4 br4_5 (
    .busW(busW), .RA(RA[1:0]), .RW(RW[1:0]), .RegWr(and_5_out), .RB(RB[1:0]), .clk(clk), .reset(reset),
    .busA(br4_5_busa), .busB(br4_5_busb));
  BR4 br4_6 (
    .busW(busW), .RA(RA[1:0]), .RW(RW[1:0]), .RegWr(and_6_out), .RB(RB[1:0]), .clk(clk), .reset(reset),
    .busA(br4_6_busa), .busB(br4_6_busb));
  BR4 br4_7 (
    .busW(busW), .RA(RA[1:0]), .RW(RW[1:0]), .RegWr(and_7_out), .RB(RB[1:0]), .clk(clk), .reset(reset),
    .busA(br4_7_busa), .busB(br4_7_busb));
  BR4 br4_8 (
    .busW(busW), .RA(RA[1:0]), .RW(RW[1:0]), .RegWr(and_8_out), .RB(RB[1:0]), .clk(clk), .reset(reset),
    .busA(br4_8_busa), .busB(br4_8_busb));
  Multiplexer #(.select(3), .width(32), .enable("false")) multiplexer_1 (
    .in0(br4_1_busa), .in1(br4_2_busa), .in2(br4_3_busa), .in3(br4_4_busa), .in4(br4_5_busa),
    .in5(br4_6_busa), .in6(br4_7_busa), .in7(br4_8_busa), .out(busA), .sel(RA[4:2]));
  Multiplexer #(.select(3), .width(32), .enable("false")) multiplexer_2 (
    .in0(br4_1_busb), .in1(br4_2_busb), .in2(br4_3_busb), .in3(br4_4_busb), .in4(br4_5_busb),
    .in5(br4_6_busb), .in6(br4_7_busb), .in7(br4_8_busb), .out(busB), .sel(RB[4:2]));

  // Other names for the same wires on the sheet: RAmux[2:0] = RA[4:2]; RAreg[1:0] = RA[1:0]; RBmux[2:0] = RB[4:2];
  //   RBreg[1:0] = RB[1:0]; RWdecod[2:0] = RW[4:2]; RWreg[1:0] = RW[1:0]
endmodule

// UC
module PROC1 (
  input  in_1
);

  wire and_1_out, AWr, BWr, clk, comparator_2_eq, CWr, IRWr, MDRWr, MemWr, muxDst, muxPC, not_1_out,
       not_2_out, PCWr, q0, q1, q2, q3, RegWr, S;
  wire [1:0] muxW;
  wire [3:0] rom_2_data;
  wire [4:0] multiplexer_2_out;
  wire [15:0] adder_1_out, multiplexer_1_out, PC_q;
  wire [31:0] adder_2_out, B, bit_extender_1_out, br32_1_busa, br32_1_busb, busA, I, MDR_q,
       multiplexer_3_out, ram_1_data, RC_q, rom_1_data;

  Multiplexer #(.width(16), .enable("false")) multiplexer_1 (
    .in0(adder_1_out), .in1(I[28:13]), .out(multiplexer_1_out), .sel(muxPC));
  Register #(.width(16)) PC (.D(multiplexer_1_out), .en(PCWr), .Q(PC_q), .clk(clk), .clr(in_1));
  Adder #(.width(16)) adder_1 (.a(16'h1), .b(PC_q), .out(adder_1_out));  // open: cin, cout
  ROM #(.addrWidth(16), .dataWidth(32)) rom_1 (.addr(PC_q), .data(rom_1_data));  // open: sel
  Clock clock_1 (.out(clk));
  Register #(.width(32)) IR (.D(rom_1_data), .en(IRWr), .Q(I), .clk(clk), .clr(in_1));
  assign bit_extender_1_out = {{16{I[28]}}, I[28:13]};  // Bit_Extender bit_extender_1
  Multiplexer #(.width(5), .enable("false")) multiplexer_2 (
    .in0(I[4:0]), .in1(I[14:10]), .out(multiplexer_2_out), .sel(muxDst));
  Multiplexer #(.select(2), .width(32), .enable("false")) multiplexer_3 (
    .in0(bit_extender_1_out), .in1(RC_q), .in2(MDR_q), .out(multiplexer_3_out), .sel(muxW));  // open: in3
  BR32 br32_1 (
    .RegWr(RegWr), .RA(I[9:5]), .RB(I[4:0]), .RW(multiplexer_2_out), .busW(multiplexer_3_out), .reset(in_1),
    .clk(clk), .busA(br32_1_busa), .busB(br32_1_busb));
  Register #(.width(32)) RA (.D(br32_1_busa), .en(AWr), .Q(busA), .clk(clk), .clr(in_1));
  Register #(.width(32)) RB (.D(br32_1_busb), .en(BWr), .Q(B), .clk(clk), .clr(in_1));
  Adder #(.width(32)) adder_2 (.a(busA), .b(B), .out(adder_2_out));  // open: cin, cout
  Comparator #(.width(32)) comparator_1 (.a(br32_1_busa), .b(br32_1_busb), .eq(S));  // open: gt, lt
  Register #(.width(32)) RC (.D(adder_2_out), .en(CWr), .Q(RC_q), .clk(clk), .clr(in_1));
  not not_1 (not_1_out, MemWr);
  Comparator #(.width(16)) comparator_2 (.a({16{1'b1}}), .b(busA[15:0]), .eq(comparator_2_eq));  // open: gt, lt
  and and_1 (and_1_out, comparator_2_eq, not_2_out);
  not not_2 (not_2_out, MemWr);
  ROM #(.dataWidth(4)) rom_2 (.addr({q3, q2, q1, q0, I[31:29], S}), .data(rom_2_data));  // open: sel
  ROM #(.addrWidth(4), .dataWidth(12)) rom_3 (
    .addr({q3, q2, q1, q0}), .data({PCWr, muxPC, IRWr, AWr, BWr, muxDst, RegWr, muxW, CWr, MemWr, MDRWr}));  // open: sel
  RAM #(.addrWidth(16), .dataWidth(32), .bus("separate")) ram_1 (
    .addr(busA[15:0]), .din(B), .data(ram_1_data), .str(not_1_out), .clk(clk), .ld(MemWr));  // open: sel, clr
  // tty_ctrl tty_ctrl_1: pin names not known
  // TTY tty_1: pin names not known; wires that end beside it: {16{1'b1}}, and_1_out, B[6:0], clk
  Register #(.width(4)) register_1 (.D(rom_2_data), .en(1'b1), .Q({q3, q2, q1, q0}), .clk(clk), .clr(in_1));
  Register #(.width(32)) MDR (.D(ram_1_data), .en(MDRWr), .Q(MDR_q), .clk(clk), .clr(in_1));

  // Other names for the same wires on the sheet: op[2:0] = I[31:29]; D[6:0] = B[6:0]; tunnel[15:0] = busA[15:0];
  //   k[15:0] = I[28:13]; SAL[11:0] = {PCWr, muxPC, IRWr, AWr, BWr, muxDst, RegWr, muxW, CWr, MemWr, MDRWr};
  //   ra[4:0] = I[9:5]; rb[4:0] = I[4:0]; rd[4:0] = I[14:10]; reset = in_1

  // Notes on the sheet:
  //   MOV
  //   ADD
  //   LD
  //   MEMi
  //   contents of rom_1 (hex, n*v repeats v):
  //   a0000005 a000c000 a0000001 a001e002 a0002003 20000843 40000044 200014a4 20000423 80016020 8000a000
  //   a0000000 60000005 a002c006 bfffe007 a009e002 a0096003 800340a6 a009c001 a0040004 600000e1 600000e2
  //   600000e4 600000e2 600000e3 80038021 600000e2 600000e3 600000e0
  //   ST
  //   BEQ
  //   NOP
  //   BR
  //   TS
  //   TT
  //   UC
  //   MEMd
  //   contents of rom_2 (hex, n*v repeats v):
  //   16*e 16*2 16*3 16*0 16*5 16*6 16*0 16*8 16*0 a b a b a b a b a b a b a b a b 64*0 d d 1 1 4 4 7 7 9
  //   9 c c
  //   contents of rom_3 (hex, n*v repeats v):
  //   202 182 6 86a 182 3 832 182 800 182 802 c02 822 802 2
  //   tty
endmodule
